// Logisim project processador-seguindo-viana.circ as structural Verilog
module adder_1b (
  input  A,
  input  CI,
  input  B,
  output S,
  output CO
);

  wire and_1_out, and_2_out, xor_1_out;

  xor xor_1 (xor_1_out, A, B);
  and and_1 (and_1_out, A, B);
  xor xor_2 (S, CI, xor_1_out);
  and and_2 (and_2_out, xor_1_out, CI);
  or or_1 (CO, and_2_out, and_1_out);

  // Notes on the sheet:
  //   LF - Adder 1b
endmodule

module adder_4b (
  input  [3:0] BusA,
  input  [3:0] BusB,
  output [4:0] _16_8_4_2_1
);

  wire adder_1b_2_co, adder_1b_3_co, adder_1b_4_co, clock_1_out;

  LED A3 (.in(BusA[3]));
  LED B3 (.in(BusB[3]));
  LED A0 (.in(BusA[0]));
  LED A1 (.in(BusA[1]));
  LED A2 (.in(BusA[2]));
  LED B0 (.in(BusB[0]));
  LED B1 (.in(BusB[1]));
  LED B2 (.in(BusB[2]));
  LED S0 (.in(_16_8_4_2_1[0]));
  LED S1 (.in(_16_8_4_2_1[1]));
  LED S2 (.in(_16_8_4_2_1[2]));
  LED S3 (.in(_16_8_4_2_1[3]));
  adder_1b adder_1b_1 (.CI(adder_1b_2_co), .A(BusA[3]), .B(BusB[3]), .S(_16_8_4_2_1[3]), .CO(_16_8_4_2_1[4]));
  adder_1b adder_1b_2 (.CI(adder_1b_3_co), .A(BusA[2]), .B(BusB[2]), .S(_16_8_4_2_1[2]), .CO(adder_1b_2_co));
  adder_1b adder_1b_3 (.CI(adder_1b_4_co), .A(BusA[1]), .B(BusB[1]), .S(_16_8_4_2_1[1]), .CO(adder_1b_3_co));
  adder_1b adder_1b_4 (.CI(clock_1_out), .A(BusA[0]), .B(BusB[0]), .S(_16_8_4_2_1[0]), .CO(adder_1b_4_co));
  Clock clock_1 (.out(clock_1_out));

  // Notes on the sheet:
  //   8 4 2 1
  //   8 4 2 1
  //   LF - Adder 4b
endmodule
